# Fritzing sketch Smart RC Car (saved by Fritzing 0.9.3b)
breadboards: 1

parts:
  Part1 = Arduino Uno (Rev3) - ICSP
  M1 = DC Motor
  VCC1 = Battery
  IC1 = L293D [package=THT]
  M2 = DC Motor
  M3 = DC Motor
  M4 = DC Motor
  hc-sr1 = hc-sr04
  LED1 = LED - 5mm [color="Red (633nm)" package="5 mm [THT]"]
  LED2 = LED - 5mm [color="Red (633nm)" package="5 mm [THT]"]
  R1 = Resistor [tolerance=±5% resistance=220 package=THT]
  R5 = Resistor [tolerance=±5% resistance=220 package=THT]
  IR1 = TSOP312.., 314.. [package=THT]
  R6 = Resistor [tolerance=±5% resistance=10k package=THT]

nets:
  GND: Part1.GND, VCC1.-, IC1.0V, hc-sr1.GND, LED1.anode, LED2.anode, IR1.Vs
  N1: Part1.D9_PWM, IC1.In_2
  N2: Part1.D10_PWM/SS, IC1.In_1
  N3: Part1.D11_PWM/MOSI, IC1.Enable_1
  N4: Part1.D12/MISO, hc-sr1.Trig
  N5: Part1.D13/SCK, IR1.GND, R6.Pin_0
  N6: Part1.D3_PWM, IC1.In_4
  N7: Part1.D5_PWM, IC1.In_3
  N8: Part1.D6_PWM, hc-sr1.Echo
  N9: Part1.D7, IC1.Enable_2
  5V: Part1.5V, IC1.+V, hc-sr1.VCC, R1.Pin_1, IR1.Data, R6.Pin_1
  N10: M1.pin_1, IC1.Out_1_(_Controlled_by_Enable_1_), M2.pin_1
  N11: M1.pin_2, IC1.Out_2_(_Controlled_by_Enable_1_), M2.pin_2
  N12: VCC1.+, IC1.+Vmotor
  N13: IC1.Out_3_(_Controlled_by_Enable_2_), M3.pin_1, M4.pin_1
  N14: IC1.Out_4_(_Controlled_by_Enable_2_), M3.pin_2, M4.pin_2
  N15: LED1.cathode, R1.Pin_0
  N16: LED2.cathode, R5.Pin_0

notes:
  4 Motors attatched to wheels
  Headlights
  Ultrasonic Sensor for Automatic braking
  IR receiver to receiver IR signals
  9v batteries to power the motors
